// Digital circuit CPU 4.dig as structural Verilog
module CPU_4 (
  input  clk,
  output CLK1,
  output CLK2
);

  wire _74245_1_p13, _74245_1_p14, _74245_1_p15, _74245_1_p16, _74245_1_p17, _74245_1_p18, _74245_1_p19,
       _74245_1_p20, and_1_out, and_2_out, and_3_out, and_5_out, and_6_out, and_7_out, and_8_out, and_9_out,
       bussplitter_1_d0, bussplitter_1_d1, bussplitter_1_d2, bussplitter_1_d3, bussplitter_1_d4,
       bussplitter_1_d5, bussplitter_1_d6, bussplitter_1_d7, CARRY, d_ff_as_1_q, d_ff_as_2_q,
       demultiplexer_1_out_0, demultiplexer_1_out_1, demultiplexer_2_out_1, demultiplexer_2_out_2,
       demultiplexer_2_out_3, demultiplexer_2_out_4, demultiplexer_2_out_5, demultiplexer_2_out_6,
       demultiplexer_2_out_7, demultiplexer_3_out_0, demultiplexer_3_out_1, demultiplexer_4_out_1,
       demultiplexer_4_out_2, demultiplexer_4_out_3, demultiplexer_4_out_4, demultiplexer_5_out_0,
       demultiplexer_5_out_1, demultiplexer_6_out_0, demultiplexer_6_out_1, demultiplexer_6_out_2, EQUAL,
       FP_INC, FP_JMP, FP_JMP0, FP_RUN, FP_STEP, FP_STEP0, FP_STR, HALT, JMP_C, JMP_E, JMP_EN, JMP_SEL,
       MEMDATA, multiplexer_1_out, nA_DOUT, nA_ST, nDISPH_ST, nDISPL_ST, nIMM_DOUT, nMARH_ST, nMARL_ST,
       nMEM_DOUT, nMEM_ST, nOP_ST, not_1_out, not_4_out, not_14_out, not_19_out, not_20_out, not_21_out,
       not_25_out, not_26_out, not_27_out, nPC_init, nPC_jmp, nPC_ST, nPCH_ST, nSUM_DOUT, nSUM_ST, nTERM,
       or_2_out, or_5_out, or_6_out, t_ff_1_nq, t_ff_1_q;
  wire [1:0] alu4_1_p7;
  wire [2:0] DOUT;
  wire [3:0] DISP_H_q, DISP_H_q_2, DISP_L_q, DISP_L_q_2, ST;
  wire [7:0] A_q, alu4_1_p5, CTRL_q, CTRL_q_2, d_ff_1_q, d_ff_1_q_2, d_ff_2_q, DATA, dipswitch_8_out,
       MEM__32k_d, OP_q, SUM_q;
  wire [7:7] MAR_H_q_2;
  wire [14:0] MAR_H_q;
  wire [15:0] IWORD, PC_out;
  wire [15:8] PC_H_q;

  LED BR1 (.in(d_ff_1_q_2[7]));
  LED BR0 (.in(d_ff_1_q_2[6]));
  LED ST2 (.in(d_ff_1_q_2[5]));
  LED ST1 (.in(d_ff_1_q_2[4]));
  LED ST0 (.in(d_ff_1_q_2[3]));
  and and_1 (and_1_out, nPC_ST, ~FP_JMP);  // And
  and and_2 (and_2_out, ~JMP_C, ~CARRY);  // And
  and and_3 (and_3_out, ~JMP_E, EQUAL);  // And
  not not_1 (not_1_out, nPC_init);
  LED DT2 (.in(d_ff_1_q_2[2]));
  LED DT1 (.in(d_ff_1_q_2[1]));
  Register #(.Bits(8)) PC_H (.D(DATA), .C(CLK2), .en(nPCH_ST), .Q(PC_H_q));
  or or_1 (JMP_EN, and_2_out, and_3_out);
  Demultiplexer demultiplexer_1 (
    .sel(JMP_SEL), .in(not_1_out), .out_0(demultiplexer_1_out_0), .out_1(demultiplexer_1_out_1));
  not not_2 (JMP_C, demultiplexer_1_out_0);
  not not_3 (JMP_E, demultiplexer_1_out_1);
  or or_2 (or_2_out, nPC_init, JMP_EN);
  LED DT0 (.in(d_ff_1_q_2[0]));
  or or_3 (nPC_ST, or_2_out, nPC_jmp);
  LED IM7 (.in(d_ff_1_q[7]));
  LED IM6 (.in(d_ff_1_q[6]));
  DipSwitch dipswitch_1 (.out(dipswitch_8_out[7]));
  DipSwitch dipswitch_2 (.out(dipswitch_8_out[6]));
  CounterPreset #(.Bits(16)) PC (
    .en(~FP_JMP), .C(CLK2), .dir(1'b0), .in({PC_H_q, DATA}), .ld(~and_1_out), .clr(1'b0), .out(PC_out));  // open: ovf
  LED IM5 (.in(d_ff_1_q[5]));
  LED IM4 (.in(d_ff_1_q[4]));
  DipSwitch dipswitch_3 (.out(dipswitch_8_out[5]));
  DipSwitch dipswitch_4 (.out(dipswitch_8_out[4]));
  Demultiplexer #(.Selector_Bits(3)) demultiplexer_2 (
    .sel(ST[2:0]), .in(not_4_out), .out_1(demultiplexer_2_out_1), .out_2(demultiplexer_2_out_2),
    .out_3(demultiplexer_2_out_3), .out_4(demultiplexer_2_out_4), .out_5(demultiplexer_2_out_5),
    .out_6(demultiplexer_2_out_6), .out_7(demultiplexer_2_out_7));  // open: out_0
  not not_4 (not_4_out, ST[3]);
  Demultiplexer #(.Selector_Bits(3)) demultiplexer_3 (
    .sel(ST[2:0]), .in(ST[3]), .out_0(demultiplexer_3_out_0), .out_1(demultiplexer_3_out_1));  // open: out_2, out_3, out_4, out_5, out_6, out_7
  LED IM3 (.in(d_ff_1_q[3]));
  LED IM2 (.in(d_ff_1_q[2]));
  DipSwitch dipswitch_5 (.out(dipswitch_8_out[3]));
  DipSwitch dipswitch_6 (.out(dipswitch_8_out[2]));
  ROM #(.AddrBits(16), .Bits(16)) rom_1 (.A(PC_out), .sel(1'b1), .D(IWORD));
  not not_5 (nA_ST, demultiplexer_2_out_1);
  not not_6 (nMEM_ST, demultiplexer_2_out_2);
  not not_7 (nSUM_ST, demultiplexer_2_out_3);
  not not_8 (nMARL_ST, demultiplexer_2_out_4);
  not not_9 (nMARH_ST, demultiplexer_2_out_5);
  not not_10 (nPCH_ST, demultiplexer_2_out_6);
  not not_11 (nOP_ST, demultiplexer_2_out_7);
  not not_12 (nPC_init, demultiplexer_3_out_0);
  not not_13 (nPC_jmp, demultiplexer_3_out_1);
  LED IM1 (.in(d_ff_1_q[1]));
  LED IM0 (.in(d_ff_1_q[0]));
  DipSwitch dipswitch_7 (.out(dipswitch_8_out[1]));
  DipSwitch dipswitch_8 (.out(dipswitch_8_out[0]));
  assign DATA = ~not_14_out ? dipswitch_8_out : 8'bz;  // DriverInvSel driverinvsel_1
  D_FF #(.Bits(16)) d_ff_1 (.D(IWORD), .C(~CLK2), .Q({d_ff_1_q_2, d_ff_1_q}));  // open: nQ
  D_FF #(.Bits(16)) CTRL (.D(IWORD), .C(CLK1), .Q({CTRL_q_2, CTRL_q}));  // open: nQ
  not not_14 (not_14_out, FP_JMP);
  Demultiplexer #(.Selector_Bits(3)) demultiplexer_4 (
    .sel(DOUT), .in(1'b1), .out_1(demultiplexer_4_out_1), .out_2(demultiplexer_4_out_2),
    .out_3(demultiplexer_4_out_3), .out_4(demultiplexer_4_out_4));  // open: out_0, out_5, out_6, out_7
  LED D7 (.in(d_ff_2_q[7]));
  LED D6 (.in(d_ff_2_q[6]));
  PullDown pulldown_1 (.out(FP_RUN));
  PullDown pulldown_2 (.out(FP_STEP0));
  DipSwitch RUN (.out(FP_RUN));
  DipSwitch STEP (.out(FP_STEP0));
  PullDown #(.Bits(8)) pulldown_3 (.out({JMP_SEL, ST, DOUT}));
  assign {JMP_SEL, ST, DOUT} = ~HALT ? CTRL_q_2 : 8'bz;  // DriverInvSel driverinvsel_2
  not not_15 (nA_DOUT, demultiplexer_4_out_1);
  not not_16 (nMEM_DOUT, demultiplexer_4_out_2);
  not not_17 (nSUM_DOUT, demultiplexer_4_out_3);
  not not_18 (nIMM_DOUT, demultiplexer_4_out_4);
  LED D5 (.in(d_ff_2_q[5]));
  LED D4 (.in(d_ff_2_q[4]));
  PullDown pulldown_4 (.out(FP_JMP0));
  PullDown pulldown_5 (.out(FP_STR));
  DipSwitch JMP (.out(FP_JMP0));
  DipSwitch STR (.out(FP_STR));
  assign DATA = ~nIMM_DOUT ? CTRL_q : 8'bz;  // DriverInvSel driverinvsel_3
  LED D3 (.in(d_ff_2_q[3]));
  LED D2 (.in(d_ff_2_q[2]));
  PullDown pulldown_6 (.out(FP_INC));
  DipSwitch INC (.out(FP_INC));
  LED D1 (.in(d_ff_2_q[1]));
  LED D0 (.in(d_ff_2_q[0]));
  D_FF #(.Bits(8)) d_ff_2 (.D(DATA), .C(~CLK2), .Q(d_ff_2_q));  // open: nQ
  not not_19 (not_19_out, nTERM);
  and and_4 (FP_JMP, FP_JMP0, ~FP_RUN);  // And
  PullDown #(.Bits(8)) pulldown_7 (.out(DATA));
  not not_20 (not_20_out, OP_q[6]);
  Demultiplexer demultiplexer_5 (
    .sel(nMEM_ST), .in(not_19_out), .out_0(demultiplexer_5_out_0), .out_1(demultiplexer_5_out_1));
  D_FF_AS d_ff_as_1 (.Set(1'b0), .D(FP_STEP), .C(~CLK1), .Clr(~FP_STEP), .Q(d_ff_as_1_q));  // open: nQ
  Register #(.Bits(8)) A (.D(DATA), .C(CLK2), .en(~nA_ST), .Q(A_q));
  Register #(.Bits(8)) OP (.D(DATA), .C(CLK2), .en(~nOP_ST), .Q(OP_q));
  Multiplexer multiplexer_1 (.sel(OP_q[7]), .in_0(not_20_out), .in_1(CARRY), .out(multiplexer_1_out));
  Register #(.Bits(8)) MAR_L (.D(DATA), .C(CLK2), .en(~nMARL_ST), .Q(MAR_H_q[7:0]));
  Register #(.Bits(8)) MAR_H (.D(DATA), .C(CLK2), .en(~nMARH_ST), .Q({MAR_H_q_2[7], MAR_H_q[14:8]}));
  and and_5 (and_5_out, FP_STEP, ~d_ff_as_1_q);  // And
  Terminal #(.termWidth(80), .termHeight(24)) terminal_1 (.D(DATA), .C(CLK2), .en(demultiplexer_5_out_0));
  Keyboard keyboard_1 (.C(CLK2), .en(demultiplexer_5_out_1), .D(MEMDATA));  // open: av
  or or_4 (FP_STEP, FP_STEP0, FP_JMP, FP_INC);
  or or_5 (or_5_out, FP_RUN, and_5_out);
  assign DATA = ~nA_DOUT ? A_q : 8'bz;  // DriverInvSel driverinvsel_4
  and and_6 (and_6_out, nMEM_ST, nMEM_DOUT);
  and and_7 (and_7_out, or_5_out, ~clk);  // And
  // ALU4 alu4_1: pin names not known; wires that end beside it: A_q, DATA, OP_q[4:0], multiplexer_1_out, alu4_1_p5, alu4_1_p7[1], alu4_1_p7[0]
  D_FF_AS d_ff_as_2 (.Set(and_7_out), .D(1'b0), .C(~CLK2), .Clr(1'b0), .Q(d_ff_as_2_q));  // open: nQ
  or or_6 (or_6_out, MAR_H_q_2[7], 1'b0);
  Demultiplexer #(.Selector_Bits(3)) demultiplexer_6 (
    .sel(MAR_H_q[2:0]), .in(and_8_out), .out_0(demultiplexer_6_out_0), .out_1(demultiplexer_6_out_1),
    .out_2(demultiplexer_6_out_2));  // open: out_3, out_4, out_5, out_6, out_7
  and and_8 (and_8_out, ~and_6_out, MAR_H_q_2[7]);  // And
  not not_21 (not_21_out, d_ff_as_2_q);
  not not_22 (nDISPL_ST, demultiplexer_6_out_0);
  not not_23 (nDISPH_ST, demultiplexer_6_out_1);
  not not_24 (nTERM, demultiplexer_6_out_2);
  and and_9 (and_9_out, clk, d_ff_as_2_q);
  or or_7 (HALT, FP_JMP, FP_INC, not_21_out);
  RAMSinglePortSel #(.AddrBits(15), .Bits(8)) MEM__32k (
    .A(MAR_H_q), .CS(~or_6_out), .WE(~nMEM_ST), .OE(~nMEM_DOUT), .D(MEM__32k_d));
  PullDown #(.Bits(8)) pulldown_8 (.out(MEM__32k_d));
  not not_25 (not_25_out, nMEM_DOUT);
  PullDown pulldown_9 (.out(and_9_out));
  not not_26 (not_26_out, and_9_out);
  not not_27 (not_27_out, nMEM_DOUT);
  BusSplitter #(.Bits(8)) bussplitter_1 (
    .D(MEM__32k_d), .OE(not_25_out), .D0(bussplitter_1_d0), .D1(bussplitter_1_d1), .D2(bussplitter_1_d2),
    .D3(bussplitter_1_d3), .D4(bussplitter_1_d4), .D5(bussplitter_1_d5), .D6(bussplitter_1_d6),
    .D7(bussplitter_1_d7));
  Seven_Seg_Hex seven_seg_hex_1 (.d(DISP_H_q_2), .dp(1'b0));
  Register #(.Bits(8)) DISP_H (.D(DATA), .C(CLK2), .en(~nDISPH_ST), .Q({DISP_H_q_2, DISP_H_q}));
  Register #(.Bits(8)) DISP_L (.D(DATA), .C(CLK2), .en(~nDISPL_ST), .Q({DISP_L_q_2, DISP_L_q}));
  T_FF #(.withEnable("false")) t_ff_1 (.C(not_26_out), .Q(t_ff_1_q), .nQ(t_ff_1_nq));
  // _74245 _74245_1: pin names not known; wires that end beside it: not_27_out, 1'b1, 1'b0, bussplitter_1_d0, bussplitter_1_d1, bussplitter_1_d2, bussplitter_1_d3, bussplitter_1_d4, bussplitter_1_d5, bussplitter_1_d6, bussplitter_1_d7, 1'b0, _74245_1_p13, _74245_1_p14, _74245_1_p15, _74245_1_p16, _74245_1_p17, _74245_1_p18, _74245_1_p19, _74245_1_p20
  Seven_Seg_Hex seven_seg_hex_2 (.d(DISP_H_q), .dp(1'b0));
  and and_10 (CLK1, and_9_out, t_ff_1_q);
  and and_11 (CLK2, t_ff_1_nq, and_9_out);
  Register #(.Bits(2)) CE (.D(alu4_1_p7), .C(CLK2), .en(~nSUM_ST), .Q({EQUAL, CARRY}));
  Register #(.Bits(8)) SUM (.D(alu4_1_p5), .C(CLK2), .en(~nSUM_ST), .Q(SUM_q));
  Seven_Seg_Hex seven_seg_hex_3 (.d(DISP_L_q_2), .dp(1'b0));
  PullDown pulldown_10 (.out(_74245_1_p20));
  PullDown pulldown_11 (.out(_74245_1_p19));
  PullDown pulldown_12 (.out(_74245_1_p18));
  Seven_Seg_Hex seven_seg_hex_4 (.d(DISP_L_q), .dp(1'b0));
  assign DATA = ~nSUM_DOUT ? SUM_q : 8'bz;  // DriverInvSel driverinvsel_5
  PullDown pulldown_13 (.out(_74245_1_p17));
  PullDown pulldown_14 (.out(_74245_1_p16));
  PullDown pulldown_15 (.out(_74245_1_p15));
  PullDown pulldown_16 (.out(_74245_1_p14));
  BusSplitter #(.Bits(8)) bussplitter_2 (
    .D(DATA), .OE(nMEM_DOUT), .D0(_74245_1_p13), .D1(_74245_1_p14), .D2(_74245_1_p15), .D3(_74245_1_p16),
    .D4(_74245_1_p17), .D5(_74245_1_p18), .D6(_74245_1_p19), .D7(_74245_1_p20));
  PullDown pulldown_17 (.out(_74245_1_p13));

  // Other names for the same wires on the sheet: CLK_1 = CLK1; CLK_2 = CLK2

  // Notes on the sheet:
  //   clk: Hz: 10
  //   PANEL0
  //   ATLAS PDC-8
  //   CTRL0
  //   CTRL1
  //   contents of rom_1 (hex, n*v repeats v):
  //   2c80,2402,1448,1445,144c,144c,144f,1452,144c,1444
  //   IO
  //   PANEL1
  //   ALU
  //   MEM
endmodule
